// Logisim project Gray_to_Binary_Convertor.circ as structural Verilog: 1 circuit, main circuit main
module main (
  input  B3,
  input  B2,
  input  B1,
  input  B0,
  output G3,
  output G2,
  output G1,
  output G0
);

  xor XOR1 (G2, B3, B2);
  xor XOR2 (G1, G2, B1);
  xor XOR3 (G0, G1, B0);

  assign G3 = B3;
endmodule
